# Fritzing sketch Project (saved by Fritzing 0.9.3b)
breadboards: 1

parts:
  Part1 = Arduino Uno (Rev3)
  LCD1 = LCD screen
  R1 = Trimmer Potentiometer [maximum_resistance=10kΩ package=THT]
  R2 = Resistor [tolerance=±5% resistance=230 package=THT]
  Logic_Level_Converter = Logic Level Converter
  WeMos_D1_Mini1 = WeMos D1 Mini

nets:
  N1: Part1.D11_PWM/MOSI, LCD1.E
  N2: Part1.D12/MISO, LCD1.RS
  GND: Part1.GND, LCD1.VSS, LCD1.R/W, LCD1.LED-, R1.leg1, Logic_Level_Converter.GND, WeMos_D1_Mini1.G
  N3: Part1.D0/RX, Logic_Level_Converter.TX2_HV
  N4: Part1.D2, LCD1.DB7
  N5: Part1.D3_PWM, LCD1.DB6
  N6: Part1.D4, LCD1.DB5
  N7: Part1.D5_PWM, LCD1.DB4
  5V: Part1.5V, LCD1.VDD, R1.leg2, R2.Pin_1, Logic_Level_Converter.HV, WeMos_D1_Mini1.5V
  N8: LCD1.V0, R1.wiper
  N9: LCD1.LED+, R2.Pin_0
  N10: Logic_Level_Converter.TX2_LV, WeMos_D1_Mini1.TX
  N11: Logic_Level_Converter.LV, WeMos_D1_Mini1.3V3
